// Logisim project CPU.circ as structural Verilog: 7 circuits, main circuit ALU
module ALU (
  input  [15:0] A,
  input  [15:0] B,
  input  [3:0] AluOp,
  output [15:0] ALUoutput,
  output Flag
);

  wire comparator_1_lt, multiplexer_1_out;
  wire [15:0] adder_1_out, and_1_out, multiplexer_2_out, multiplexer_3_out, multiplexer_4_out, not_1_out,
       or_1_out, shifter_1_out, shifter_2_out, shifter_3_out, shifter_4_out, SltOut, SltuOut,
       subtractor_1_out, subtractor_2_out, xor_1_out;

  assign and_1_out = A & B;  // AND_Gate and_1, 16 bits wide
  assign or_1_out = A | B;  // OR_Gate or_1, 16 bits wide
  assign xor_1_out = A ^ B;  // XOR_Gate xor_1, 16 bits wide
  Shifter #(.width(16)) shifter_1 (.in(A), .\dist (B[3:0]), .out(shifter_1_out));
  Shifter #(.shift("rl"), .width(16)) shifter_2 (.in(A), .\dist (B[3:0]), .out(shifter_2_out));
  Shifter #(.shift("lr"), .width(16)) shifter_3 (.in(A), .\dist (B[3:0]), .out(shifter_3_out));
  Shifter #(.shift("ar"), .width(16)) shifter_4 (.in(A), .\dist (B[3:0]), .out(shifter_4_out));
  assign SltuOut = {{15{1'b0}}, comparator_1_lt};  // Bit_Extender bit_extender_1
  Comparator #(.mode("unsigned"), .width(16)) comparator_1 (.a(A), .b(B), .lt(comparator_1_lt));  // open: gt, eq
  Subtractor #(.width(16)) subtractor_1 (.a(A), .b(B), .out(subtractor_1_out));  // open: bin, bout
  Adder #(.width(16)) adder_1 (.a(A), .b(B), .out(adder_1_out));  // open: cin, cout
  Subtractor #(.width(16)) subtractor_2 (.a(A), .b(B), .out(subtractor_2_out));  // open: bin, bout
  assign not_1_out = ~or_1_out;  // NOT_Gate not_1, 16 bits wide
  Multiplexer #(.select(4)) multiplexer_1 (
    .in0(subtractor_1_out[15]), .in1(subtractor_1_out[14]), .in2(subtractor_1_out[13]),
    .in3(subtractor_1_out[12]), .in4(subtractor_1_out[11]), .in5(subtractor_1_out[10]),
    .in6(subtractor_1_out[9]), .in7(subtractor_1_out[8]), .in8(subtractor_1_out[7]),
    .in9(subtractor_1_out[6]), .in10(subtractor_1_out[5]), .in11(subtractor_1_out[4]),
    .in12(subtractor_1_out[3]), .in13(subtractor_1_out[2]), .in14(subtractor_1_out[1]),
    .in15(subtractor_1_out[0]), .out(multiplexer_1_out), .sel(4'b0000));
  Multiplexer #(.select(2), .width(16)) multiplexer_2 (
    .in0(shifter_1_out), .in1(shifter_2_out), .in2(shifter_3_out), .in3(shifter_4_out),
    .out(multiplexer_2_out), .sel(AluOp[1:0]));
  Multiplexer #(.select(2), .width(16)) multiplexer_3 (
    .in0(and_1_out), .in1(or_1_out), .in2(not_1_out), .in3(xor_1_out), .out(multiplexer_3_out),
    .sel(AluOp[1:0]));
  assign SltOut = {{15{1'b0}}, multiplexer_1_out};  // Bit_Extender bit_extender_2
  Multiplexer #(.select(2), .width(16)) multiplexer_4 (
    .in0(adder_1_out), .in1(subtractor_2_out), .in2(SltOut), .in3(SltuOut), .out(multiplexer_4_out),
    .sel(AluOp[1:0]));
  Multiplexer #(.select(2), .width(16)) multiplexer_5 (
    .in0(multiplexer_2_out), .in1(multiplexer_3_out), .in2(multiplexer_4_out), .out(ALUoutput),
    .sel(AluOp[3:2]));  // open: in3
  Comparator #(.mode("unsigned"), .width(16)) comparator_2 (.a(ALUoutput), .b({16{1'b0}}), .eq(Flag));  // open: gt, lt

  // Other names for the same wires on the sheet: func[1:0] = AluOp[1:0]; SelType[1:0] = AluOp[3:2]
endmodule

module Main (
);

  wire AluSrc, clock_1_out, memRd, memRw, RegWr, zeroF;
  wire [1:0] PCsrc, RegDs, WBdata;
  wire [2:0] Func, multiplexer_2_out, register_8_q, register_11_q, register_13_q, splriterr_rd, splriterr_rs,
       splriterr_rt;
  wire [3:0] AluOpp, OpCodee;
  wire [5:0] splriterr_imm6;
  wire [11:0] adder_2_out, bit_extender_1_out, JALIns, LUI, multiplexer_1_out, register_1_q, register_2_q,
       register_4_q, register_6_q;
  wire [15:0] ALuu_aluoutput, bit_extender_2_out, bit_extender_3_out, bit_extender_4_out, multiplexer_3_out,
       multiplexer_4_out, ram_1_dout, register_3_q, register_5_q, register_7_q, register_9_q, register_10_q,
       register_12_q, registerfile_1_busa, registerfile_1_busb, rom_1_data, shifter_1_out;
  wire [15:12] register_6_q_2;

  Multiplexer #(.select(2), .width(12)) multiplexer_1 (
    .in0(JALIns), .in1(LUI), .in2(register_4_q), .in3(register_6_q), .out(multiplexer_1_out), .sel(PCsrc));
  Clock clock_1 (.out(clock_1_out));
  Register #(.width(12)) register_1 (.D(multiplexer_1_out), .Q(register_1_q), .clk(clock_1_out));  // open: en, clr
  Adder #(.width(12)) adder_1 (.a(12'h1), .b(register_1_q), .out(JALIns));  // open: cin, cout
  ROM #(.addrWidth(12), .dataWidth(16)) rom_1 (.addr(register_1_q), .data(rom_1_data));
  PcControl pccontrol_1 (.op(OpCodee), .Func(Func), .zeroF(zeroF), .PCsrc(PCsrc));
  Register #(.width(12)) register_2 (.D(JALIns), .Q(register_2_q), .clk(clock_1_out));  // open: en, clr
  Register #(.width(16)) register_3 (.D(rom_1_data), .Q(register_3_q), .clk(clock_1_out));  // open: en, clr
  Spliter splriterr (
    .instr(register_3_q), .OpCode(OpCodee), .Imm12(LUI), .Rs(splriterr_rs), .Imm6(splriterr_imm6),
    .Rt(splriterr_rt), .Func(Func), .Rd(splriterr_rd));
  assign bit_extender_1_out = {{6{splriterr_imm6[5]}}, splriterr_imm6};  // Bit_Extender bit_extender_1
  assign bit_extender_2_out = {{10{splriterr_imm6[5]}}, splriterr_imm6};  // Bit_Extender bit_extender_2
  Adder #(.width(12)) adder_2 (.a(register_2_q), .b(bit_extender_1_out), .out(adder_2_out));  // open: cin, cout
  Multiplexer #(.select(2), .width(3)) multiplexer_2 (
    .in0(splriterr_rt), .in1(splriterr_rd), .in2(3'b111), .in3(3'b001), .out(multiplexer_2_out), .sel(RegDs));
  mainControl maincontrol_1 (
    .op(OpCodee), .Func(Func), .RegWrite(RegWr), .RegDst(RegDs), .AluSrc(AluSrc), .MemRead(memRd),
    .MemWrite(memRw), .WbData(WBdata));  // open: PCsrc
  registerFile registerfile_1 (
    .RW(register_13_q), .RegWrite(RegWr), .BusW(register_12_q), .Clock(clock_1_out), .RA(splriterr_rs),
    .RB(splriterr_rt), .BusB(registerfile_1_busb), .BusA(registerfile_1_busa));
  Register #(.width(12)) register_4 (.D(adder_2_out), .Q(register_4_q), .clk(clock_1_out));  // open: en, clr
  Register #(.width(16)) register_5 (.D(bit_extender_2_out), .Q(register_5_q), .clk(clock_1_out));  // open: en, clr
  Register #(.width(16)) register_6 (
    .D(registerfile_1_busa), .Q({register_6_q_2, register_6_q}), .clk(clock_1_out));  // open: en, clr
  Register #(.width(16)) register_7 (.D(registerfile_1_busb), .Q(register_7_q), .clk(clock_1_out));  // open: en, clr
  Register #(.width(3)) register_8 (.D(multiplexer_2_out), .Q(register_8_q), .clk(clock_1_out));  // open: en, clr
  Multiplexer #(.width(16)) multiplexer_3 (
    .in0(register_7_q), .in1(register_5_q), .out(multiplexer_3_out), .sel(AluSrc));
  ALU ALuu (
    .AluOp(AluOpp), .A({register_6_q_2, register_6_q}), .B(multiplexer_3_out), .ALUoutput(ALuu_aluoutput),
    .Flag(zeroF));
  AluControl alucontrol_1 (.op(OpCodee), .Func(Func), .AluOp(AluOpp));
  Register #(.width(16)) register_9 (.D(ALuu_aluoutput), .Q(register_9_q), .clk(clock_1_out));  // open: en, clr
  Register #(.width(16)) register_10 (.D(register_7_q), .Q(register_10_q), .clk(clock_1_out));  // open: en, clr
  Register #(.width(3)) register_11 (.D(register_8_q), .Q(register_11_q), .clk(clock_1_out));  // open: en, clr
  RAM #(.addrWidth(12), .dataWidth(16), .trigger("falling")) ram_1 (
    .addr(register_9_q[11:0]), .we(memRw), .oe(memRd), .clk(clock_1_out), .din(register_10_q),
    .dout(ram_1_dout));
  assign bit_extender_3_out = {{4{1'b0}}, JALIns};  // Bit_Extender bit_extender_3
  assign bit_extender_4_out = {{4{1'b0}}, LUI};  // Bit_Extender bit_extender_4
  Shifter #(.width(16)) shifter_1 (.in(bit_extender_4_out), .\dist (4'b0100), .out(shifter_1_out));
  Multiplexer #(.select(2), .width(16)) multiplexer_4 (
    .in0(register_9_q), .in1(ram_1_dout), .in2(bit_extender_3_out), .in3(shifter_1_out),
    .out(multiplexer_4_out), .sel(WBdata));
  Register #(.width(16)) register_12 (.D(multiplexer_4_out), .Q(register_12_q), .clk(clock_1_out));  // open: en, clr
  Register #(.width(3)) register_13 (.D(register_11_q), .Q(register_13_q), .clk(clock_1_out));  // open: en, clr

  // Notes on the sheet:
  //   contents of rom_1 (hex, n*v repeats v):
  //   f005 8305 d006 80ff c004 c005 8089 c7 c008
endmodule

module registerFile (
  input  [2:0] RB,
  input  [2:0] RA,
  input  [2:0] RW,
  input  RegWrite,
  input  [15:0] BusW,
  input  Clock,
  output [15:0] BusB,
  output [15:0] BusA
);

  wire and_1_out, and_2_out, and_3_out, and_4_out, and_5_out, and_6_out, and_7_out, decoder_1_out1,
       decoder_1_out2, decoder_1_out3, decoder_1_out4, decoder_1_out5, decoder_1_out6, decoder_1_out7,
       decoder_2_out0, decoder_2_out1, decoder_2_out2, decoder_2_out3, decoder_2_out4, decoder_2_out5,
       decoder_2_out6, decoder_2_out7, decoder_3_out0, decoder_3_out1, decoder_3_out2, decoder_3_out3,
       decoder_3_out4, decoder_3_out5, decoder_3_out6, decoder_3_out7;
  wire [15:0] register_1_q, register_2_q, register_3_q, register_4_q, register_5_q, register_6_q,
       register_7_q;

  Decoder #(.enable("false"), .select(3)) decoder_1 (
    .out1(decoder_1_out1), .out2(decoder_1_out2), .out3(decoder_1_out3), .out4(decoder_1_out4),
    .out5(decoder_1_out5), .out6(decoder_1_out6), .out7(decoder_1_out7), .sel(RW));  // open: out0
  and and_1 (and_1_out, decoder_1_out1, RegWrite);
  and and_2 (and_2_out, decoder_1_out2, RegWrite);
  and and_3 (and_3_out, decoder_1_out3, RegWrite);
  and and_4 (and_4_out, decoder_1_out4, RegWrite);
  and and_5 (and_5_out, decoder_1_out5, RegWrite);
  and and_6 (and_6_out, decoder_1_out6, RegWrite);
  and and_7 (and_7_out, decoder_1_out7, RegWrite);
  Register #(.width(16)) register_1 (.D(BusW), .en(and_1_out), .Q(register_1_q), .clk(Clock));  // open: clr
  Register #(.width(16)) register_2 (.D(BusW), .en(and_2_out), .Q(register_2_q), .clk(Clock));  // open: clr
  Register #(.width(16)) register_3 (.D(BusW), .en(and_3_out), .Q(register_3_q), .clk(Clock));  // open: clr
  Register #(.width(16)) register_4 (.D(BusW), .en(and_4_out), .Q(register_4_q), .clk(Clock));  // open: clr
  Register #(.width(16)) register_5 (.D(BusW), .en(and_5_out), .Q(register_5_q), .clk(Clock));  // open: clr
  Register #(.width(16)) register_6 (.D(BusW), .en(and_6_out), .Q(register_6_q), .clk(Clock));  // open: clr
  Register #(.width(16)) register_7 (.D(BusW), .en(and_7_out), .Q(register_7_q), .clk(Clock));  // open: clr
  Decoder #(.enable("false"), .select(3)) decoder_2 (
    .out0(decoder_2_out0), .out1(decoder_2_out1), .out2(decoder_2_out2), .out3(decoder_2_out3),
    .out4(decoder_2_out4), .out5(decoder_2_out5), .out6(decoder_2_out6), .out7(decoder_2_out7), .sel(RA));
  assign BusA = decoder_2_out1 ? register_1_q : 16'bz;  // Controlled_Buffer controlled_buffer_1
  assign BusA = decoder_2_out2 ? register_2_q : 16'bz;  // Controlled_Buffer controlled_buffer_2
  assign BusA = decoder_2_out3 ? register_3_q : 16'bz;  // Controlled_Buffer controlled_buffer_3
  assign BusA = decoder_2_out4 ? register_4_q : 16'bz;  // Controlled_Buffer controlled_buffer_4
  assign BusA = decoder_2_out5 ? register_5_q : 16'bz;  // Controlled_Buffer controlled_buffer_5
  assign BusA = decoder_2_out6 ? register_6_q : 16'bz;  // Controlled_Buffer controlled_buffer_6
  assign BusA = decoder_2_out7 ? register_7_q : 16'bz;  // Controlled_Buffer controlled_buffer_7
  assign BusA = decoder_2_out0 ? {16{1'b0}} : 16'bz;  // Controlled_Buffer controlled_buffer_8
  Decoder #(.enable("false"), .select(3)) decoder_3 (
    .out0(decoder_3_out0), .out1(decoder_3_out1), .out2(decoder_3_out2), .out3(decoder_3_out3),
    .out4(decoder_3_out4), .out5(decoder_3_out5), .out6(decoder_3_out6), .out7(decoder_3_out7), .sel(RB));
  assign BusB = decoder_3_out1 ? register_1_q : 16'bz;  // Controlled_Buffer controlled_buffer_9
  assign BusB = decoder_3_out2 ? register_2_q : 16'bz;  // Controlled_Buffer controlled_buffer_10
  assign BusB = decoder_3_out3 ? register_3_q : 16'bz;  // Controlled_Buffer controlled_buffer_11
  assign BusB = decoder_3_out4 ? register_4_q : 16'bz;  // Controlled_Buffer controlled_buffer_12
  assign BusB = decoder_3_out5 ? register_5_q : 16'bz;  // Controlled_Buffer controlled_buffer_13
  assign BusB = decoder_3_out6 ? register_6_q : 16'bz;  // Controlled_Buffer controlled_buffer_14
  assign BusB = decoder_3_out7 ? register_7_q : 16'bz;  // Controlled_Buffer controlled_buffer_15
  assign BusB = decoder_3_out0 ? {16{1'b0}} : 16'bz;  // Controlled_Buffer controlled_buffer_16
endmodule

module Spliter (
  input  [15:0] instr,
  output [2:0] Func,
  output [5:0] Imm6,
  output [3:0] OpCode,
  output [2:0] Rd,
  output [2:0] Rs,
  output [2:0] Rt,
  output [11:0] Imm12
);


  assign Func = instr[2:0];
  assign Imm6 = instr[5:0];
  assign Imm12 = instr[11:0];
  assign OpCode = instr[15:12];
  assign Rd = instr[5:3];
  assign Rs = instr[11:9];
  assign Rt = instr[8:6];
endmodule

module AluControl (
  input  [3:0] op,
  input  [2:0] Func,
  output [3:0] AluOp
);

  wire and_1_out, and_2_out, and_3_out, and_4_out, and_5_out, and_6_out, and_7_out, and_8_out, not_1_out,
       not_2_out, not_3_out, not_4_out;

  not not_1 (not_1_out, op[3]);
  not not_2 (not_2_out, op[2]);
  not not_3 (not_3_out, op[1]);
  not not_4 (not_4_out, op[0]);
  and and_1 (and_1_out, not_2_out, op[0]);
  and and_2 (and_2_out, op[2], not_3_out);
  and and_3 (and_3_out, not_1_out, not_3_out, Func[2]);
  and and_4 (and_4_out, not_1_out, not_2_out, Func[1]);
  and and_5 (and_5_out, not_2_out, op[1], not_4_out);
  and and_6 (and_6_out, not_1_out, not_2_out, Func[0]);
  and and_7 (and_7_out, op[3], op[0]);
  and and_8 (and_8_out, op[2], not_3_out, op[0]);
  or or_1 (AluOp[3], and_1_out, op[1], op[3]);
  or or_2 (AluOp[2], and_2_out, and_3_out);
  or or_3 (AluOp[1], and_4_out, and_5_out);
  or or_4 (AluOp[0], and_6_out, and_7_out, and_8_out);
endmodule

module mainControl (
  input  [3:0] op,
  input  [2:0] Func,
  output RegWrite,
  output [1:0] RegDst,
  output AluSrc,
  output MemRead,
  output MemWrite,
  output [1:0] WbData,
  output [1:0] PCsrc
);

  wire and_1_out, and_2_out, and_3_out, and_4_out, and_5_out, and_7_out, and_8_out, and_9_out, and_14_out,
       and_15_out, and_16_out, and_17_out, not_1_out, not_2_out, not_3_out, not_4_out, not_5_out;

  not not_1 (not_1_out, op[3]);
  not not_2 (not_2_out, op[2]);
  not not_3 (not_3_out, op[1]);
  not not_4 (not_4_out, op[0]);
  not not_5 (not_5_out, Func[2]);
  and and_1 (and_1_out, not_2_out, not_4_out);
  and and_2 (and_2_out, not_1_out, not_3_out, not_5_out);
  and and_3 (and_3_out, not_1_out, not_4_out);
  and and_4 (and_4_out, op[3], op[2], op[0]);
  and and_5 (and_5_out, not_1_out, op[2], not_3_out);
  and and_6 (RegDst[1], op[3], op[0]);
  and and_7 (and_7_out, not_1_out, not_2_out);
  and and_8 (and_8_out, op[1], op[0]);
  and and_9 (and_9_out, op[3], not_4_out);
  and and_10 (MemRead, not_1_out, op[1], not_4_out);
  and and_11 (MemWrite, not_1_out, op[1], op[0]);
  and and_12 (WbData[1], op[3], op[0]);
  and and_13 (WbData[0], op[2], op[1]);
  and and_14 (and_14_out, op[3], not_2_out, op[0]);
  and and_15 (and_15_out, not_2_out, op[0], Func[2]);
  and and_16 (and_16_out, op[3], op[2], not_3_out);
  and and_17 (and_17_out, not_1_out, not_2_out, op[0], Func[2]);
  or or_1 (RegWrite, and_1_out, and_2_out, and_3_out, and_4_out, and_5_out);
  or or_2 (RegDst[0], and_7_out, and_8_out);
  or or_3 (AluSrc, and_9_out, op[2]);
  or or_4 (PCsrc[1], and_14_out, and_15_out);
  or or_5 (PCsrc[0], and_16_out, and_17_out);
endmodule

module PcControl (
  input  [3:0] op,
  input  [2:0] Func,
  input  zeroF,
  output [1:0] PCsrc
);

  wire and_1_out, and_2_out, and_3_out, and_4_out, and_5_out, not_1_out, not_2_out, not_3_out, not_4_out;

  not not_1 (not_1_out, op[3]);
  not not_2 (not_2_out, op[2]);
  not not_3 (not_3_out, op[1]);
  not not_4 (not_4_out, zeroF);
  and and_1 (and_1_out, not_2_out, op[1], op[0], not_4_out);
  and and_2 (and_2_out, op[3], not_2_out, not_3_out, op[0], zeroF);
  and and_3 (and_3_out, not_1_out, not_2_out, op[0], Func[2]);
  and and_4 (and_4_out, op[3], op[2], not_3_out);
  and and_5 (and_5_out, not_1_out, not_2_out, op[0], Func[2]);
  or or_1 (PCsrc[1], and_1_out, and_2_out, and_3_out);
  or or_2 (PCsrc[0], and_4_out, and_5_out);
endmodule
