// Logisim project CPU_Design.circ as structural Verilog: 12 circuits, main circuit ALU
module ALU (
  input  [15:0] A,
  input  [15:0] B,
  input  [3:0] AluOp,
  output [15:0] ALUoutput,
  output Flag
);

  wire comparator_1_lt, multiplexer_1_out;
  wire [15:0] adder_1_out, and_1_out, multiplexer_2_out, multiplexer_3_out, multiplexer_4_out, not_1_out,
       or_1_out, shifter_1_out, shifter_2_out, shifter_3_out, shifter_4_out, SltOut, SltuOut,
       subtractor_1_out, subtractor_2_out, xor_1_out;

  assign and_1_out = A & B;  // AND_Gate and_1, 16 bits wide
  assign or_1_out = A | B;  // OR_Gate or_1, 16 bits wide
  assign xor_1_out = A ^ B;  // XOR_Gate xor_1, 16 bits wide
  Shifter #(.width(16)) shifter_1 (.in(A), .\dist (B[3:0]), .out(shifter_1_out));
  Shifter #(.shift("rl"), .width(16)) shifter_2 (.in(A), .\dist (B[3:0]), .out(shifter_2_out));
  Shifter #(.shift("lr"), .width(16)) shifter_3 (.in(A), .\dist (B[3:0]), .out(shifter_3_out));
  Shifter #(.shift("ar"), .width(16)) shifter_4 (.in(A), .\dist (B[3:0]), .out(shifter_4_out));
  assign SltuOut = {{15{1'b0}}, comparator_1_lt};  // Bit_Extender bit_extender_1
  Comparator #(.mode("unsigned"), .width(16)) comparator_1 (.a(A), .b(B), .lt(comparator_1_lt));  // open: gt, eq
  Subtractor #(.width(16)) subtractor_1 (.a(A), .b(B), .out(subtractor_1_out));  // open: bin, bout
  Adder #(.width(16)) adder_1 (.a(A), .b(B), .out(adder_1_out));  // open: cin, cout
  Subtractor #(.width(16)) subtractor_2 (.a(A), .b(B), .out(subtractor_2_out));  // open: bin, bout
  assign not_1_out = ~or_1_out;  // NOT_Gate not_1, 16 bits wide
  Multiplexer #(.select(4)) multiplexer_1 (
    .in0(subtractor_1_out[15]), .in1(subtractor_1_out[14]), .in2(subtractor_1_out[13]),
    .in3(subtractor_1_out[12]), .in4(subtractor_1_out[11]), .in5(subtractor_1_out[10]),
    .in6(subtractor_1_out[9]), .in7(subtractor_1_out[8]), .in8(subtractor_1_out[7]),
    .in9(subtractor_1_out[6]), .in10(subtractor_1_out[5]), .in11(subtractor_1_out[4]),
    .in12(subtractor_1_out[3]), .in13(subtractor_1_out[2]), .in14(subtractor_1_out[1]),
    .in15(subtractor_1_out[0]), .out(multiplexer_1_out), .sel(4'b0000));
  Multiplexer #(.select(2), .width(16)) multiplexer_2 (
    .in0(shifter_1_out), .in1(shifter_2_out), .in2(shifter_3_out), .in3(shifter_4_out),
    .out(multiplexer_2_out), .sel(AluOp[1:0]));
  Multiplexer #(.select(2), .width(16)) multiplexer_3 (
    .in0(and_1_out), .in1(or_1_out), .in2(not_1_out), .in3(xor_1_out), .out(multiplexer_3_out),
    .sel(AluOp[1:0]));
  assign SltOut = {{15{1'b0}}, multiplexer_1_out};  // Bit_Extender bit_extender_2
  Multiplexer #(.select(2), .width(16)) multiplexer_4 (
    .in0(adder_1_out), .in1(subtractor_2_out), .in2(SltOut), .in3(SltuOut), .out(multiplexer_4_out),
    .sel(AluOp[1:0]));
  Multiplexer #(.select(2), .width(16)) multiplexer_5 (
    .in0(multiplexer_2_out), .in1(multiplexer_3_out), .in2(multiplexer_4_out), .out(ALUoutput),
    .sel(AluOp[3:2]));  // open: in3
  Comparator #(.mode("unsigned"), .width(16)) comparator_2 (.a(ALUoutput), .b({16{1'b0}}), .eq(Flag));  // open: gt, lt

  // Other names for the same wires on the sheet: func[1:0] = AluOp[1:0]; SelType[1:0] = AluOp[3:2]
endmodule

module Main (
);

  wire AluSrc, and_1_out, and_2_out, Beq, Bne, clock_1_out, comparator_1_eq, comparator_2_eq,
       comparator_3_eq, comparator_4_eq, comparator_5_eq, Dedected, ExMeMRd, J, Jr, Kill1, Kill2, memRd,
       memRw, not_1_out, not_2_out, not_3_out, or_1_out, or_2_out, RegWr2, RegWr3, RegWr4, Stall, zeroF;
  wire [1:0] FB, PCsrc, RegDs, WBdata;
  wire [2:0] Dedc, FA, Func, multiplexer_3_out, Rd3, Rd4, Rs, Rt, splriterr_rd;
  wire [3:0] AluOpp, EAluOp, EEluOp, OpCodee;
  wire [4:0] ex_control_reg_1_memout;
  wire [5:0] splriterr_imm6;
  wire [11:0] adder_2_out, bit_extender_1_out, JALIns, LUI, multiplexer_1_out, multiplexer_6_out,
       register_1_q, register_2_q, register_6_q, register_9_q;
  wire [11:4] maincontrol_pipe_1_alusrc;
  wire [15:0] Alur, bit_extender_2_out, bit_extender_3_out, bit_extender_4_out, LUIR, MemR,
       multiplexer_2_out, multiplexer_4_out, multiplexer_5_out, multiplexer_7_out, ram_1_dout, register_3_q,
       register_7_q, register_8_q, register_10_q, register_11_q, register_13_q, register_14_q, register_15_q,
       register_17_q, registerfile_1_busa, registerfile_1_busb, rom_1_data, shifter_1_out, WbR;
  wire [15:12] register_9_q_2;

  Multiplexer #(.select(2), .width(12)) multiplexer_1 (
    .in0(JALIns), .in1(LUI), .in2(register_6_q), .in3(register_9_q), .out(multiplexer_1_out), .sel(PCsrc));
  Clock clock_1 (.out(clock_1_out));
  Register #(.width(12)) register_1 (
    .D(multiplexer_1_out), .en(not_1_out), .Q(register_1_q), .clk(clock_1_out));  // open: clr
  not not_1 (not_1_out, Stall);
  Adder #(.width(12)) adder_1 (.a(12'h1), .b(register_1_q), .out(JALIns));  // open: cin, cout
  ROM #(.addrWidth(12), .dataWidth(16)) rom_1 (.addr(register_1_q), .data(rom_1_data));
  PcPipline pcpipline_1 (
    .J(J), .BNE(Bne), .BEQ(Beq), .Zero(zeroF), .JR(Jr), .PCSrc(PCsrc), .Kill1(Kill1), .Kill2(Kill2));
  Multiplexer #(.width(16)) multiplexer_2 (.in0(rom_1_data), .in1({16{1'b0}}), .out(multiplexer_2_out), .sel(Kill1));
  not not_2 (not_2_out, Stall);
  Register #(.width(12)) register_2 (.D(JALIns), .Q(register_2_q), .clk(clock_1_out));  // open: en, clr
  Register #(.width(16)) register_3 (
    .D(multiplexer_2_out), .en(not_2_out), .Q(register_3_q), .clk(clock_1_out));  // open: clr
  Spliter splriterr (
    .instr(register_3_q), .OpCode(OpCodee), .Imm12(LUI), .Rs(Rs), .Imm6(splriterr_imm6), .Rt(Rt),
    .Func(Func), .Rd(splriterr_rd));
  Register #(.width(4)) register_4 (.D(OpCodee), .Q(EEluOp), .clk(clock_1_out));  // open: en, clr
  mainControl_PIPE maincontrol_pipe_1 (
    .op(OpCodee), .Func(Func), .RegWrite(maincontrol_pipe_1_alusrc[9]), .RegDst(RegDs),
    .AluSrc(maincontrol_pipe_1_alusrc[4]), .MemRead(maincontrol_pipe_1_alusrc[5]),
    .MemWrite(maincontrol_pipe_1_alusrc[6]), .WbData(maincontrol_pipe_1_alusrc[8:7]), .J(J),
    .BEQ(maincontrol_pipe_1_alusrc[10]), .BNE(maincontrol_pipe_1_alusrc[11]), .Jr(Jr));
  assign bit_extender_1_out = {{6{splriterr_imm6[5]}}, splriterr_imm6};  // Bit_Extender bit_extender_1
  assign bit_extender_2_out = {{10{splriterr_imm6[5]}}, splriterr_imm6};  // Bit_Extender bit_extender_2
  AluControl alucontrol_1 (.op(OpCodee), .Func(Func), .AluOp(AluOpp));
  Adder #(.width(12)) adder_2 (.a(register_2_q), .b(bit_extender_1_out), .out(adder_2_out));  // open: cin, cout
  Multiplexer #(.select(2), .width(3)) multiplexer_3 (
    .in0(Rt), .in1(splriterr_rd), .in2(3'b111), .in3(3'b001), .out(multiplexer_3_out), .sel(RegDs));
  registerFile registerfile_1 (
    .RW(Rd4), .RegWrite(RegWr4), .BusW(WbR), .Clock(clock_1_out), .RA(Rs), .RB(Rt),
    .BusB(registerfile_1_busb), .BusA(registerfile_1_busa));
  Register #(.width(3)) register_5 (.D(multiplexer_3_out), .Q(Dedc), .clk(clock_1_out));  // open: en, clr
  Forward forward_1 (
    .Rt(Rt), .Rs(Rs), .Rd4(Rd4), .Rd3(Rd3), .Rd2(Dedc), .RegWr2(RegWr2), .RegWr3(RegWr3), .RegWr4(RegWr4),
    .EXMemRd(ExMeMRd), .EAlu(EEluOp), .Alun(OpCodee), .Func(Func), .Dedc(Dedc), .out_14(Dedected), .FA(FA),
    .FB(FB), .Stall(Stall));
  Register #(.width(12)) register_6 (.D(adder_2_out), .Q(register_6_q), .clk(clock_1_out));  // open: en, clr
  Multiplexer #(.select(3), .width(16)) multiplexer_4 (
    .in0(registerfile_1_busa), .in1(Alur), .in2(MemR), .in3(WbR), .in4(LUIR), .out(multiplexer_4_out),
    .sel(FA));  // open: in5, in6, in7
  Multiplexer #(.select(2), .width(16)) multiplexer_5 (
    .in0(registerfile_1_busb), .in1(Alur), .in2(MemR), .in3(WbR), .out(multiplexer_5_out), .sel(FB));
  Register #(.width(16)) register_7 (.D(multiplexer_5_out), .Q(register_7_q), .clk(clock_1_out));  // open: en, clr
  or or_1 (or_1_out, Kill2, Stall);
  Register #(.width(16)) register_8 (.D(bit_extender_2_out), .Q(register_8_q), .clk(clock_1_out));  // open: en, clr
  Register #(.width(16)) register_9 (
    .D(multiplexer_4_out), .Q({register_9_q_2, register_9_q}), .clk(clock_1_out));  // open: en, clr
  Multiplexer #(.width(12)) multiplexer_6 (
    .in0({maincontrol_pipe_1_alusrc, AluOpp}), .in1({12{1'b0}}), .out(multiplexer_6_out), .sel(or_1_out));
  EX_Control_Reg ex_control_reg_1 (
    .EXIN(multiplexer_6_out), .clk(clock_1_out), .ALUOp(EAluOp), .ALUSrc(AluSrc), .EMeMRd(ExMeMRd),
    .MEMOut(ex_control_reg_1_memout), .BEQo(Beq), .RegWr2(RegWr2), .BNEo(Bne));
  Multiplexer #(.width(16)) multiplexer_7 (
    .in0(register_7_q), .in1(register_8_q), .out(multiplexer_7_out), .sel(AluSrc));
  ALU ALuu (.AluOp(EAluOp), .A({register_9_q_2, register_9_q}), .B(multiplexer_7_out), .ALUoutput(Alur), .Flag(zeroF));
  Comparator #(.mode("unsigned"), .width(3)) comparator_1 (.a(Func), .b(3'b111), .eq(comparator_1_eq));  // open: gt, lt
  Comparator #(.mode("unsigned"), .width(3)) comparator_2 (.a(Rs), .b(3'b001), .eq(comparator_2_eq));  // open: gt, lt
  Register #(.width(16)) register_10 (.D(Alur), .Q(register_10_q), .clk(clock_1_out));  // open: en, clr
  Register #(.width(16)) register_11 (.D(register_7_q), .Q(register_11_q), .clk(clock_1_out));  // open: en, clr
  Register #(.width(3)) register_12 (.D(Dedc), .Q(Rd3), .clk(clock_1_out));  // open: en, clr
  Comparator #(.mode("unsigned"), .width(4)) comparator_3 (
    .a(EAluOp), .b(4'b1111), .eq(comparator_3_eq));  // open: gt, lt
  Comparator #(.mode("unsigned"), .width(4)) comparator_4 (
    .a(AluOpp), .b(4'b0000), .eq(comparator_4_eq));  // open: gt, lt
  Comparator #(.mode("unsigned"), .width(4)) comparator_5 (
    .a(AluOpp), .b(4'b0001), .eq(comparator_5_eq));  // open: gt, lt
  not not_3 (not_3_out, comparator_1_eq);
  RAM #(.addrWidth(12), .dataWidth(16), .trigger("falling")) ram_1 (
    .addr(register_10_q[11:0]), .we(memRw), .oe(memRd), .clk(clock_1_out), .din(register_11_q),
    .dout(ram_1_dout));
  MEM mem_1 (
    .MEMIn(ex_control_reg_1_memout), .clk(clock_1_out), .memR(memRd), .memWr(memRw), .Wbdata(WBdata),
    .RegWr(RegWr3));
  and and_1 (and_1_out, comparator_5_eq, not_3_out);
  assign bit_extender_3_out = {{4{1'b0}}, JALIns};  // Bit_Extender bit_extender_3
  assign bit_extender_4_out = {{4{1'b0}}, LUI};  // Bit_Extender bit_extender_4
  Register #(.width(16)) register_13 (.D(bit_extender_3_out), .Q(register_13_q), .clk(clock_1_out));  // open: en, clr
  Shifter #(.width(16)) shifter_1 (.in(bit_extender_4_out), .\dist (4'b0100), .out(shifter_1_out));
  or or_2 (or_2_out, comparator_4_eq, and_1_out);
  Register #(.width(16)) register_14 (.D(register_13_q), .Q(register_14_q), .clk(clock_1_out));  // open: en, clr
  Register #(.width(16)) register_15 (.D(register_14_q), .Q(register_15_q), .clk(clock_1_out));  // open: en, clr
  Register #(.width(16)) register_16 (.D(shifter_1_out), .Q(LUIR), .clk(clock_1_out));  // open: en, clr
  Register #(.width(16)) register_17 (.D(LUIR), .Q(register_17_q), .clk(clock_1_out));  // open: en, clr
  Register #(.width(1)) WB (.D(RegWr3), .Q(RegWr4), .clk(clock_1_out));  // open: en, clr
  and and_2 (and_2_out, comparator_3_eq, or_2_out, comparator_2_eq);
  Multiplexer #(.select(2), .width(16)) multiplexer_8 (
    .in0(register_10_q), .in1(ram_1_dout), .in2(register_15_q), .in3(register_17_q), .out(MemR), .sel(WBdata));
  Register #(.width(3)) register_18 (.D(Rd3), .Q(Rd4), .clk(clock_1_out));  // open: en, clr
  Register #(.width(16)) register_19 (.D(MemR), .Q(WbR), .clk(clock_1_out));  // open: en, clr

  // Other names for the same wires on the sheet: Rd2[2:0] = Dedc

  // Notes on the sheet:
  //   contents of rom_1 (hex, n*v repeats v):
  //   f001 5285 80ca 14e0 18e9 974 afd c008 c008
endmodule

module registerFile (
  input  [2:0] RB,
  input  [2:0] RA,
  input  [2:0] RW,
  input  RegWrite,
  input  [15:0] BusW,
  input  Clock,
  output [15:0] BusB,
  output [15:0] BusA
);

  wire and_1_out, and_2_out, and_3_out, and_4_out, and_5_out, and_6_out, and_7_out, decoder_1_out1,
       decoder_1_out2, decoder_1_out3, decoder_1_out4, decoder_1_out5, decoder_1_out6, decoder_1_out7,
       decoder_2_out0, decoder_2_out1, decoder_2_out2, decoder_2_out3, decoder_2_out4, decoder_2_out5,
       decoder_2_out6, decoder_2_out7, decoder_3_out0, decoder_3_out1, decoder_3_out2, decoder_3_out3,
       decoder_3_out4, decoder_3_out5, decoder_3_out6, decoder_3_out7;
  wire [15:0] register_1_q, register_2_q, register_3_q, register_4_q, register_5_q, register_6_q,
       register_7_q;

  Decoder #(.enable("false"), .select(3)) decoder_1 (
    .out1(decoder_1_out1), .out2(decoder_1_out2), .out3(decoder_1_out3), .out4(decoder_1_out4),
    .out5(decoder_1_out5), .out6(decoder_1_out6), .out7(decoder_1_out7), .sel(RW));  // open: out0
  and and_1 (and_1_out, decoder_1_out1, RegWrite);
  and and_2 (and_2_out, decoder_1_out2, RegWrite);
  and and_3 (and_3_out, decoder_1_out3, RegWrite);
  and and_4 (and_4_out, decoder_1_out4, RegWrite);
  and and_5 (and_5_out, decoder_1_out5, RegWrite);
  and and_6 (and_6_out, decoder_1_out6, RegWrite);
  and and_7 (and_7_out, decoder_1_out7, RegWrite);
  Register #(.width(16)) register_1 (.D(BusW), .en(and_1_out), .Q(register_1_q), .clk(Clock));  // open: clr
  Register #(.width(16)) register_2 (.D(BusW), .en(and_2_out), .Q(register_2_q), .clk(Clock));  // open: clr
  Register #(.width(16)) register_3 (.D(BusW), .en(and_3_out), .Q(register_3_q), .clk(Clock));  // open: clr
  Register #(.width(16)) register_4 (.D(BusW), .en(and_4_out), .Q(register_4_q), .clk(Clock));  // open: clr
  Register #(.width(16)) register_5 (.D(BusW), .en(and_5_out), .Q(register_5_q), .clk(Clock));  // open: clr
  Register #(.width(16)) register_6 (.D(BusW), .en(and_6_out), .Q(register_6_q), .clk(Clock));  // open: clr
  Register #(.width(16)) register_7 (.D(BusW), .en(and_7_out), .Q(register_7_q), .clk(Clock));  // open: clr
  Decoder #(.enable("false"), .select(3)) decoder_2 (
    .out0(decoder_2_out0), .out1(decoder_2_out1), .out2(decoder_2_out2), .out3(decoder_2_out3),
    .out4(decoder_2_out4), .out5(decoder_2_out5), .out6(decoder_2_out6), .out7(decoder_2_out7), .sel(RA));
  assign BusA = decoder_2_out1 ? register_1_q : 16'bz;  // Controlled_Buffer controlled_buffer_1
  assign BusA = decoder_2_out2 ? register_2_q : 16'bz;  // Controlled_Buffer controlled_buffer_2
  assign BusA = decoder_2_out3 ? register_3_q : 16'bz;  // Controlled_Buffer controlled_buffer_3
  assign BusA = decoder_2_out4 ? register_4_q : 16'bz;  // Controlled_Buffer controlled_buffer_4
  assign BusA = decoder_2_out5 ? register_5_q : 16'bz;  // Controlled_Buffer controlled_buffer_5
  assign BusA = decoder_2_out6 ? register_6_q : 16'bz;  // Controlled_Buffer controlled_buffer_6
  assign BusA = decoder_2_out7 ? register_7_q : 16'bz;  // Controlled_Buffer controlled_buffer_7
  assign BusA = decoder_2_out0 ? {16{1'b0}} : 16'bz;  // Controlled_Buffer controlled_buffer_8
  Decoder #(.enable("false"), .select(3)) decoder_3 (
    .out0(decoder_3_out0), .out1(decoder_3_out1), .out2(decoder_3_out2), .out3(decoder_3_out3),
    .out4(decoder_3_out4), .out5(decoder_3_out5), .out6(decoder_3_out6), .out7(decoder_3_out7), .sel(RB));
  assign BusB = decoder_3_out1 ? register_1_q : 16'bz;  // Controlled_Buffer controlled_buffer_9
  assign BusB = decoder_3_out2 ? register_2_q : 16'bz;  // Controlled_Buffer controlled_buffer_10
  assign BusB = decoder_3_out3 ? register_3_q : 16'bz;  // Controlled_Buffer controlled_buffer_11
  assign BusB = decoder_3_out4 ? register_4_q : 16'bz;  // Controlled_Buffer controlled_buffer_12
  assign BusB = decoder_3_out5 ? register_5_q : 16'bz;  // Controlled_Buffer controlled_buffer_13
  assign BusB = decoder_3_out6 ? register_6_q : 16'bz;  // Controlled_Buffer controlled_buffer_14
  assign BusB = decoder_3_out7 ? register_7_q : 16'bz;  // Controlled_Buffer controlled_buffer_15
  assign BusB = decoder_3_out0 ? {16{1'b0}} : 16'bz;  // Controlled_Buffer controlled_buffer_16
endmodule

module Spliter (
  input  [15:0] instr,
  output [2:0] Func,
  output [5:0] Imm6,
  output [3:0] OpCode,
  output [2:0] Rd,
  output [2:0] Rs,
  output [2:0] Rt,
  output [11:0] Imm12
);


  assign Func = instr[2:0];
  assign Imm6 = instr[5:0];
  assign Imm12 = instr[11:0];
  assign OpCode = instr[15:12];
  assign Rd = instr[5:3];
  assign Rs = instr[11:9];
  assign Rt = instr[8:6];
endmodule

module AluControl (
  input  [3:0] op,
  input  [2:0] Func,
  output [3:0] AluOp
);

  wire and_1_out, and_2_out, and_3_out, and_4_out, and_5_out, and_6_out, and_7_out, and_8_out, not_1_out,
       not_2_out, not_3_out, not_4_out;

  not not_1 (not_1_out, op[3]);
  not not_2 (not_2_out, op[2]);
  not not_3 (not_3_out, op[1]);
  not not_4 (not_4_out, op[0]);
  and and_1 (and_1_out, not_2_out, op[0]);
  and and_2 (and_2_out, op[2], not_3_out);
  and and_3 (and_3_out, not_1_out, not_3_out, Func[2]);
  and and_4 (and_4_out, not_1_out, not_2_out, Func[1]);
  and and_5 (and_5_out, not_2_out, op[1], not_4_out);
  and and_6 (and_6_out, not_1_out, not_2_out, Func[0]);
  and and_7 (and_7_out, op[3], op[0]);
  and and_8 (and_8_out, op[2], not_3_out, op[0]);
  or or_1 (AluOp[3], and_1_out, op[1], op[3]);
  or or_2 (AluOp[2], and_2_out, and_3_out);
  or or_3 (AluOp[1], and_4_out, and_5_out);
  or or_4 (AluOp[0], and_6_out, and_7_out, and_8_out);
endmodule

module mainControl (
  input  [3:0] op,
  input  [2:0] Func,
  output RegWrite,
  output [1:0] RegDst,
  output AluSrc,
  output MemRead,
  output MemWrite,
  output [1:0] WbData,
  output [1:0] PCsrc
);

  wire and_1_out, and_2_out, and_3_out, and_4_out, and_5_out, and_7_out, and_8_out, and_9_out, and_14_out,
       and_15_out, and_16_out, and_17_out, not_1_out, not_2_out, not_3_out, not_4_out, not_5_out;

  not not_1 (not_1_out, op[3]);
  not not_2 (not_2_out, op[2]);
  not not_3 (not_3_out, op[1]);
  not not_4 (not_4_out, op[0]);
  not not_5 (not_5_out, Func[2]);
  and and_1 (and_1_out, not_2_out, not_4_out);
  and and_2 (and_2_out, not_1_out, not_3_out, not_5_out);
  and and_3 (and_3_out, not_1_out, not_4_out);
  and and_4 (and_4_out, op[3], op[2], op[0]);
  and and_5 (and_5_out, not_1_out, op[2], not_3_out);
  and and_6 (RegDst[1], op[3], op[0]);
  and and_7 (and_7_out, not_1_out, not_2_out);
  and and_8 (and_8_out, op[1], op[0]);
  and and_9 (and_9_out, op[3], not_4_out);
  and and_10 (MemRead, not_1_out, op[1], not_4_out);
  and and_11 (MemWrite, not_1_out, op[1], op[0]);
  and and_12 (WbData[1], op[3], op[0]);
  and and_13 (WbData[0], op[2], op[1]);
  and and_14 (and_14_out, op[3], not_2_out, op[0]);
  and and_15 (and_15_out, not_2_out, op[0], Func[2]);
  and and_16 (and_16_out, op[3], op[2], not_3_out);
  and and_17 (and_17_out, not_1_out, not_2_out, op[0], Func[2]);
  or or_1 (RegWrite, and_1_out, and_2_out, and_3_out, and_4_out, and_5_out);
  or or_2 (RegDst[0], and_7_out, and_8_out);
  or or_3 (AluSrc, and_9_out, op[2]);
  or or_4 (PCsrc[1], and_14_out, and_15_out);
  or or_5 (PCsrc[0], and_16_out, and_17_out);
endmodule

module PcControl (
  input  [3:0] op,
  input  [2:0] Func,
  input  zeroF,
  output [1:0] PCsrc
);

  wire and_1_out, and_2_out, and_3_out, and_4_out, and_5_out, not_1_out, not_2_out, not_3_out, not_4_out;

  not not_1 (not_1_out, op[3]);
  not not_2 (not_2_out, op[2]);
  not not_3 (not_3_out, op[1]);
  not not_4 (not_4_out, zeroF);
  and and_1 (and_1_out, not_2_out, op[1], op[0], not_4_out);
  and and_2 (and_2_out, op[3], not_2_out, not_3_out, op[0], zeroF);
  and and_3 (and_3_out, not_1_out, not_2_out, op[0], Func[2]);
  and and_4 (and_4_out, op[3], op[2], not_3_out);
  and and_5 (and_5_out, not_1_out, not_2_out, op[0], Func[2]);
  or or_1 (PCsrc[1], and_1_out, and_2_out, and_3_out);
  or or_2 (PCsrc[0], and_4_out, and_5_out);
endmodule

module EX_Control_Reg (
  input  [11:0] EXIN,
  input  clk,
  output [3:0] ALUOp,
  output ALUSrc,
  output EMeMRd,
  output [4:0] MEMOut,
  output BEQo,
  output RegWr2,
  output BNEo
);

  Register #(.width(1)) register_1 (.D(EXIN[10]), .Q(BEQo), .clk(clk));  // open: en, clr
  Register #(.width(1)) register_2 (.D(EXIN[11]), .Q(BNEo), .clk(clk));  // open: en, clr
  Register #(.width(1)) register_3 (.D(EXIN[5]), .Q(EMeMRd), .clk(clk));  // open: en, clr
  Register #(.width(1)) register_4 (.D(EXIN[9]), .Q(RegWr2), .clk(clk));  // open: en, clr
  Register #(.width(4)) register_5 (.D(EXIN[3:0]), .Q(ALUOp), .clk(clk));  // open: en, clr
  Register #(.width(5)) register_6 (.D(EXIN[9:5]), .Q(MEMOut), .clk(clk));  // open: en, clr
  Register #(.width(1)) register_7 (.D(EXIN[4]), .Q(ALUSrc), .clk(clk));  // open: en, clr
endmodule

module mainControl_PIPE (
  input  [3:0] op,
  input  [2:0] Func,
  output RegWrite,
  output [1:0] RegDst,
  output AluSrc,
  output MemRead,
  output MemWrite,
  output [1:0] WbData,
  output J,
  output BEQ,
  output BNE,
  output Jr
);

  wire and_1_out, and_2_out, and_3_out, and_4_out, and_5_out, and_7_out, and_8_out, and_9_out, and_14_out,
       and_15_out, and_16_out, not_1_out, not_2_out, not_3_out, not_4_out, not_5_out, not_6_out, not_7_out;

  not not_1 (not_1_out, op[3]);
  not not_2 (not_2_out, op[2]);
  not not_3 (not_3_out, op[1]);
  not not_4 (not_4_out, op[0]);
  not not_5 (not_5_out, Func[2]);
  not not_6 (not_6_out, Func[1]);
  not not_7 (not_7_out, Func[0]);
  and and_1 (and_1_out, not_2_out, not_4_out);
  and and_2 (and_2_out, not_1_out, not_3_out, not_5_out);
  and and_3 (and_3_out, not_1_out, not_4_out);
  and and_4 (and_4_out, op[3], op[2], op[0]);
  and and_5 (and_5_out, not_1_out, op[2], not_3_out);
  and and_6 (RegDst[1], op[3], op[0]);
  and and_7 (and_7_out, not_1_out, not_2_out);
  and and_8 (and_8_out, op[1], op[0]);
  and and_9 (and_9_out, op[3], not_4_out);
  and and_10 (MemRead, not_1_out, op[1], not_4_out);
  and and_11 (MemWrite, not_1_out, op[1], op[0]);
  and and_12 (WbData[1], op[3], op[0]);
  and and_13 (WbData[0], op[2], op[1]);
  and and_14 (and_14_out, op[3], op[2], not_3_out);
  and and_15 (and_15_out, not_1_out, not_2_out, not_3_out, op[0], Func[2], not_6_out);
  and and_16 (and_16_out, not_1_out, not_2_out, not_3_out, op[0], Func[2], not_7_out);
  and and_17 (BEQ, op[3], not_2_out, not_3_out, op[0]);
  and and_18 (BNE, op[3], not_2_out, op[1], op[0]);
  and and_19 (Jr, not_1_out, not_2_out, not_3_out, op[0], Func[2], Func[1], Func[0]);
  or or_1 (RegWrite, and_1_out, and_2_out, and_3_out, and_4_out, and_5_out);
  or or_2 (RegDst[0], and_7_out, and_8_out);
  or or_3 (AluSrc, and_9_out, op[2]);
  or or_4 (J, and_14_out, and_15_out, and_16_out);
endmodule

module MEM (
  input  [4:0] MEMIn,
  input  clk,
  output memR,
  output memWr,
  output [1:0] Wbdata,
  output RegWr
);

  Register #(.width(1)) register_1 (.D(MEMIn[0]), .Q(memR), .clk(clk));  // open: en, clr
  Register #(.width(1)) register_2 (.D(MEMIn[1]), .Q(memWr), .clk(clk));  // open: en, clr
  Register #(.width(2)) register_3 (.D(MEMIn[3:2]), .Q(Wbdata), .clk(clk));  // open: en, clr
  Register #(.width(1)) register_4 (.D(MEMIn[4]), .Q(RegWr), .clk(clk));  // open: en, clr
endmodule

module Forward (
  input  [2:0] Rt,
  input  [2:0] Rs,
  input  [2:0] Rd4,
  input  [2:0] Rd3,
  input  [2:0] Rd2,
  input  RegWr2,
  input  RegWr3,
  input  RegWr4,
  input  EXMemRd,
  input  [3:0] EAlu,
  input  [3:0] Alun,
  input  [2:0] Func,
  input  [2:0] Dedc,
  output out_14,
  output [2:0] FA,
  output [1:0] FB,
  output Stall
);

  wire and_1_out, and_2_out, and_3_out, and_4_out, and_5_out, and_6_out, comparator_1_eq, comparator_2_eq,
       comparator_3_eq, comparator_4_eq, comparator_5_eq, comparator_6_eq, comparator_7_eq, comparator_8_eq,
       comparator_9_eq, comparator_10_eq, comparator_11_eq, comparator_12_eq, comparator_13_eq,
       comparator_14_eq, comparator_15_eq, comparator_16_eq, comparator_17_eq, comparator_18_eq,
       comparator_19_eq, comparator_20_eq, comparator_21_eq, comparator_22_eq, comparator_23_eq,
       comparator_24_eq, comparator_25_eq, comparator_26_eq, comparator_27_eq, comparator_28_eq,
       comparator_29_eq, not_1_out, not_2_out, not_3_out, not_4_out, not_5_out, not_6_out, not_7_out,
       or_1_out, or_2_out, Rds2, Rds3, Rds4, Rdt2, Rdt3, Rdt4;
  wire [2:2] multiplexer_1_out;

  Comparator #(.mode("unsigned"), .width(4)) comparator_1 (
    .a(Alun), .b(4'b0100), .eq(comparator_1_eq));  // open: gt, lt
  Comparator #(.mode("unsigned"), .width(4)) comparator_2 (
    .a(Alun), .b(4'b0101), .eq(comparator_2_eq));  // open: gt, lt
  Comparator #(.mode("unsigned"), .width(4)) comparator_3 (
    .a(Alun), .b(4'b1000), .eq(comparator_3_eq));  // open: gt, lt
  Comparator #(.mode("unsigned"), .width(3)) comparator_4 (.a(Rs), .b(Rd3), .eq(comparator_4_eq));  // open: gt, lt
  Comparator #(.mode("unsigned"), .width(3)) comparator_5 (.a(Rs), .b(Rd4), .eq(comparator_5_eq));  // open: gt, lt
  Comparator #(.mode("unsigned"), .width(1)) comparator_6 (.a(RegWr4), .b(1'b1), .eq(comparator_6_eq));  // open: gt, lt
  Comparator #(.mode("unsigned"), .width(3)) comparator_7 (.a(Rt), .b(Rd2), .eq(comparator_7_eq));  // open: gt, lt
  Comparator #(.mode("unsigned"), .width(3)) comparator_8 (.a(Rt), .b(Rd3), .eq(comparator_8_eq));  // open: gt, lt
  Comparator #(.mode("unsigned"), .width(3)) comparator_9 (.a(Rt), .b(3'b000), .eq(comparator_9_eq));  // open: gt, lt
  Comparator #(.mode("unsigned"), .width(1)) comparator_10 (
    .a(RegWr3), .b(1'b1), .eq(comparator_10_eq));  // open: gt, lt
  Comparator #(.mode("unsigned"), .width(3)) comparator_11 (.a(Rt), .b(Rd4), .eq(comparator_11_eq));  // open: gt, lt
  Comparator #(.mode("unsigned"), .width(1)) comparator_12 (
    .a(RegWr4), .b(1'b1), .eq(comparator_12_eq));  // open: gt, lt
  Comparator #(.mode("unsigned"), .width(1)) comparator_13 (
    .a(EXMemRd), .b(1'b1), .eq(comparator_13_eq));  // open: gt, lt
  Comparator #(.mode("unsigned"), .width(3)) comparator_14 (.a(Rs), .b(Rd2), .eq(comparator_14_eq));  // open: gt, lt
  Comparator #(.mode("unsigned"), .width(3)) comparator_15 (.a(Rs), .b(3'b000), .eq(comparator_15_eq));  // open: gt, lt
  Comparator #(.mode("unsigned"), .width(1)) comparator_16 (
    .a(RegWr2), .b(1'b1), .eq(comparator_16_eq));  // open: gt, lt
  not not_1 (not_1_out, comparator_17_eq);
  Comparator #(.mode("unsigned"), .width(3)) comparator_17 (.a(Rs), .b(3'b000), .eq(comparator_17_eq));  // open: gt, lt
  Comparator #(.mode("unsigned"), .width(1)) comparator_18 (
    .a(RegWr3), .b(1'b1), .eq(comparator_18_eq));  // open: gt, lt
  Comparator #(.mode("unsigned"), .width(3)) comparator_19 (.a(Rs), .b(3'b000), .eq(comparator_19_eq));  // open: gt, lt
  not not_2 (not_2_out, comparator_20_eq);
  Comparator #(.mode("unsigned"), .width(3)) comparator_20 (.a(Rt), .b(3'b000), .eq(comparator_20_eq));  // open: gt, lt
  Comparator #(.mode("unsigned"), .width(1)) comparator_21 (
    .a(RegWr2), .b(1'b1), .eq(comparator_21_eq));  // open: gt, lt
  not not_3 (not_3_out, comparator_9_eq);
  Comparator #(.mode("unsigned"), .width(3)) comparator_22 (.a(Rt), .b(3'b000), .eq(comparator_22_eq));  // open: gt, lt
  Comparator #(.mode("unsigned"), .width(3)) comparator_23 (.a(Rs), .b(Rd2), .eq(comparator_23_eq));  // open: gt, lt
  Comparator #(.mode("unsigned"), .width(3)) comparator_24 (.a(Rt), .b(Rd2), .eq(comparator_24_eq));  // open: gt, lt
  Comparator #(.mode("unsigned"), .width(3)) comparator_25 (
    .a(Func), .b(3'b111), .eq(comparator_25_eq));  // open: gt, lt
  Comparator #(.mode("unsigned"), .width(3)) comparator_26 (.a(Rs), .b(Dedc), .eq(comparator_26_eq));  // open: gt, lt
  not not_4 (not_4_out, comparator_15_eq);
  not not_5 (not_5_out, comparator_22_eq);
  Comparator #(.mode("unsigned"), .width(4)) comparator_27 (
    .a(EAlu), .b(4'b1111), .eq(comparator_27_eq));  // open: gt, lt
  Comparator #(.mode("unsigned"), .width(4)) comparator_28 (
    .a(Alun), .b(4'b0000), .eq(comparator_28_eq));  // open: gt, lt
  Comparator #(.mode("unsigned"), .width(4)) comparator_29 (
    .a(Alun), .b(4'b0001), .eq(comparator_29_eq));  // open: gt, lt
  not not_6 (not_6_out, comparator_25_eq);
  not not_7 (not_7_out, comparator_19_eq);
  or or_1 (or_1_out, comparator_23_eq, comparator_24_eq);
  and and_1 (and_1_out, comparator_29_eq, not_6_out);
  and and_2 (and_2_out, comparator_5_eq, not_7_out, comparator_6_eq);
  and and_3 (and_3_out, comparator_8_eq, not_3_out, comparator_10_eq);
  and and_4 (and_4_out, comparator_11_eq, not_5_out, comparator_12_eq);
  and and_5 (and_5_out, comparator_14_eq, not_4_out, comparator_16_eq);
  and and_6 (and_6_out, comparator_4_eq, not_1_out, comparator_18_eq);
  and and_7 (Rdt2, comparator_7_eq, not_2_out, comparator_21_eq);
  or or_2 (or_2_out, comparator_28_eq, comparator_1_eq, comparator_2_eq, comparator_3_eq, and_1_out);
  and and_8 (Stall, comparator_13_eq, or_1_out);
  and and_9 (out_14, comparator_27_eq, or_2_out, comparator_26_eq);
  and and_10 (Rdt3, ~Rdt2, and_3_out);  // AND_Gate
  and and_11 (Rdt4, ~Rdt2, ~Rdt3, and_4_out);  // AND_Gate
  and and_12 (Rds2, ~out_14, and_5_out);  // AND_Gate
  and and_13 (Rds3, ~Rds2, ~out_14, and_6_out);  // AND_Gate
  and and_14 (Rds4, ~Rds3, ~Rds2, ~out_14, and_2_out);  // AND_Gate
  Multiplexer #(.select(3), .width(3)) multiplexer_1 (
    .in0(3'b000), .in1(3'b001), .in2(3'b010), .in3(3'b000), .in4(3'b011), .in5(3'b000), .in6(3'b000),
    .in7(3'b000), .out({multiplexer_1_out[2], FB}), .sel({Rdt4, Rdt3, Rdt2}));
  Multiplexer #(.select(4), .width(3)) multiplexer_2 (
    .in0(3'b000), .in1(3'b001), .in2(3'b010), .in3(3'b000), .in4(3'b011), .in5(3'b000), .in6(3'b000),
    .in7(3'b000), .in8(3'b100), .in9(3'b000), .in10(3'b000), .in11(3'b000), .in12(3'b000), .in13(3'b000),
    .in14(3'b000), .in15(3'b000), .out(FA), .sel({out_14, Rds4, Rds3, Rds2}));

  // Other names for the same wires on the sheet: LuiD = out_14; AluOpp[3:0] = Alun; EAluOp[3:0] = EAlu
endmodule

module PcPipline (
  input  J,
  input  BNE,
  input  BEQ,
  input  Zero,
  input  JR,
  output [1:0] PCSrc,
  output Kill1,
  output Kill2
);

  wire and_1_out, and_2_out, and_3_out, and_4_out, and_5_out, and_6_out, not_1_out, not_2_out, not_3_out;

  not not_1 (not_1_out, J);
  not not_2 (not_2_out, Zero);
  not not_3 (not_3_out, JR);
  and and_1 (and_1_out, not_1_out, BEQ, Zero);
  and and_2 (and_2_out, not_1_out, BNE, not_2_out);
  or or_1 (PCSrc[0], JR, J);
  and and_3 (and_3_out, BEQ, Zero);
  and and_4 (and_4_out, BNE, not_2_out);
  and and_5 (and_5_out, not_1_out, BEQ, Zero, not_3_out);
  and and_6 (and_6_out, not_1_out, BNE, not_2_out, not_3_out);
  or or_2 (PCSrc[1], JR, and_1_out, and_2_out);
  or or_3 (Kill1, JR, and_3_out, and_4_out, J);
  or or_4 (Kill2, and_5_out, and_6_out);
endmodule
